# Fritzing sketch esquemabueno (saved by Fritzing 0.8.7b)
circuit board: 8.46667cm x 5.64444cm
perfboards: 1

parts:
  ROBOTIS1 = ROBOTIS OpenCM-9.04 Type-B [part_number=Type-B]
  U1 = Voltage Regulator - 5V [package="TO220 [THT]"]  # not connected
  C1 = Electrolytic Capacitor [capacitance=1µF package="100 mil [THT, electrolytic]"]  # not connected
  C2 = Electrolytic Capacitor [capacitance=1µF package="100 mil [THT, electrolytic]"]  # not connected
  Parte2 = Dynamixel Ax-12 [part_number=n]
  Parte3 = Dynamixel Ax-12 [part_number=2]
  Parte4 = Dynamixel Ax-12 [part_number=1]
  J9 = female pin header, 3 pins [form="♀ (female)"]
  J1 = female pin header, 6 pins [form="♀ (female)"]
  J10 = Basic Servo
  J15 = female pin header, 5 pins [form="♀ (female)"]
  J16 = female pin header, 4 pins [form="♀ (female)"]
  J17 = Infrared Proximity Sensor
  J18 = female pin header, 3 pins [form="♀ (female)"]
  J19 = Infrared Proximity Sensor
  J20 = female pin header, 3 pins [form="♀ (female)"]
  BeagleBone1 = BeagleBone Black
  Parte1 = IMU Digital Combo Board 6DOF

nets:
  N1: ROBOTIS1.A9, J15.pin3
  N2: ROBOTIS1.VCC, J1.pin1
  N3: ROBOTIS1.GND, J1.pin2
  N4: ROBOTIS1.D24/SCL_2, BeagleBone1.no_name_yet#22
  N5: ROBOTIS1.D25/SDA_2, BeagleBone1.no_name_yet#21
  N6: ROBOTIS1.VGND_(Ax-series), Parte4.Data2
  N7: ROBOTIS1.VCC_(Ax-Series), Parte4.VCC2
  N8: ROBOTIS1.DATA_(Ax-Series), Parte4.GND2
  N9: Parte2.Data2, Parte3.Data1
  N10: Parte2.VCC2, Parte3.VCC1
  GND2: Parte2.GND2, Parte3.GND1
  N11: Parte3.Data2, Parte4.Data1
  N12: Parte3.VCC2, Parte4.VCC1
  GND2_2: Parte3.GND2, Parte4.GND1
  N13: J9.pin1, J10.pulse
  N14: J9.pin2, J10.vcc
  N15: J9.pin3, J10.gnd
  N16: J1.pin3, BeagleBone1.no_name_yet#3, BeagleBone1.no_name_yet#5
  N17: J1.pin4, BeagleBone1.no_name_yet#1
  N18: J15.pin1, BeagleBone1.no_name_yet#20
  N19: J15.pin2, BeagleBone1.no_name_yet#19
  N20: J15.pin4, BeagleBone1.no_name_yet#38
  N21: J15.pin5, BeagleBone1.no_name_yet#40
  N22: J16.pin1, Parte1.3.3V
  N23: J16.pin2, Parte1.GND
  N24: J16.pin3, Parte1.SDA
  N25: J16.pin4, Parte1.SCL
  N26: J17.Vout, J18.pin3
  N27: J17.GND, J18.pin1
  N28: J17.Vcc, J18.pin2
  N29: J19.Vout, J20.pin3
  N30: J19.GND, J20.pin1
  N31: J19.Vcc, J20.pin2

custom parts:
  ROBOTIS OpenCM-9.04 Type-B: The CM-9 is an open-source embedded board with open schematics and source codes. This board is Type B.
  Dynamixel Ax-12: Smart actuator created by the korean company ROBOTIS.
  BeagleBone Black: BeagleBone Black rev. A5B
