# Fritzing sketch shield (saved by Fritzing 0.8.7b)
perfboards: 1

parts:
  BeagleBone1 = BeagleBone Black  # not connected
  J1 = female pin header, 20 pins [form="♀ (female)"]
  J2 = female pin header, 20 pins [form="♀ (female)"]
  U1 = Voltage Regulator - 5V [package="TO220 [THT]"]
  J3 = single row smd male pin header, 23 pins [form="♂ (male)"]
  J4 = single row smd male pin header, 23 pins [form="♂ (male)"]
  J6 = female pin header, 20 pins [form="♀ (female)"]  # not connected
  J5 = single row smd male pin header, 2 pins [form="♂ (male)"]
  C3 = Electrolytic Capacitor [capacitance=1µF package="100 mil [THT, electrolytic]"]
  C4 = Electrolytic Capacitor [capacitance=1µF package="100 mil [THT, electrolytic]"]
  J7 = single row smd male pin header, 4 pins [form="♂ (male)"]
  J10 = single row smd male pin header, 4 pins [form="♂ (male)"]
  J11 = single row smd male pin header, 3 pins [form="♂ (male)"]
  ROBOTIS1 = ROBOTIS OpenCM-9.04 Type-B [part_number=Type-B]  # not connected
  R2 = Resistor [tolerance=±5% resistance=220 package=THT]
  J9 = single row smd male pin header, 4 pins [form="♂ (male)"]  # not connected
  J12 = single row smd male pin header, 1 pin [form="♂ (male)"]  # not connected
  R4 = Resistor [tolerance=±5% resistance=220 package=THT]
  R5 = Resistor [tolerance=±5% resistance=220 package=THT]
  J13 = single row smd male pin header, 3 pins [form="♂ (male)"]
  R6 = Resistor [tolerance=±5% resistance=220 package=THT]

nets:
  N1: J1.pin14, J11.pin3
  N2: J2.pin3, J3.pin11, J3.pin12
  N3: J2.pin4, J5.pin2
  N4: J2.pin16, J13.pin1
  N5: J2.pin17, U1.GND, J13.pin3
  N6: U1.input_voltage, C3.+, J13.pin2
  N7: U1.output_voltage, J11.pin2
  N8: J3.pin3, C4.-
  N9: J3.pin9, J3.pin10
  N10: J3.pin18, R2.Pin_1, R6.Pin_1
  N11: J3.pin19, R4.Pin_1, R5.Pin_1
  N12: J4.pin1, J11.pin1
  N13: C3.-, C4.+
  N14: J7.pin1, R2.Pin_0
  N15: J7.pin2, J10.pin2
  N16: J7.pin3, J10.pin3, R4.Pin_0, R6.Pin_0
  N17: J10.pin1, R5.Pin_0

custom parts:
  BeagleBone Black: BeagleBone Black rev. A5B
  ROBOTIS OpenCM-9.04 Type-B: The CM-9 is an open-source embedded board with open schematics and source codes. This board is Type B.
